# Fritzing sketch Schema (saved by Fritzing 0.9.3b)
breadboards: 1

parts:
  Raspberry_Pi_1 = Raspberry Pi 3 [part_number=RPI-3-V1.2]
  S1 = Momentary Switch [package=ksa_sealed_tac_switch]
  LED1 = smd LED [color="Red (633nm)" package="1206 [SMD]"]
  R1 = Resistor [tolerance=±5% resistance=220 package="0805 [SMD]"]
  R2 = Resistor [tolerance=±5% resistance=10k package="0805 [SMD]"]

nets:
  N1: Raspberry_Pi_1.3v3, R2.Pin_0
  N2: Raspberry_Pi_1.GIPO4, LED1.anode
  N3: Raspberry_Pi_1.GIPO24, S1.2, R2.Pin_1
  N4: Raspberry_Pi_1.GND, S1.4, R1.Pin_1
  N5: LED1.cathode, R1.Pin_0
